# Fritzing sketch Thermistor (Temperature Measurement) (saved by Fritzing 0.9.3b)
breadboards: 1

parts:
  Part1 = Arduino Uno (Rev3)
  R1 = Temperature Sensor (Thermistor) [thermistor_type=NTC package=THT]
  R3 = Resistor [tolerance=±5% resistance=10k package="2010 [SMD]"]

nets:
  N1: Part1.A0, R1.pin_1, R3.Pin_0
  N2: Part1.5V, R3.Pin_1
  N3: Part1.GND, R1.pin_0
